# Fritzing sketch freeze_1 (saved by Fritzing 0.9.9b)
breadboards: 1

parts:
  Composant1 = Arduino Mega 2560 (Rev3)
  U1 = ESP8266 WiFi Module [part_number=ESP8266]
  Grove1 = Grove OLED 128x96
  Grove2 = Grove OLED 128x96
  U3 = GAS_SENSOR [package=mq-3]
  T1 = TMP36 Temperature Sensor [package="TO92 [THT]"]
  Mod1 = Passive Buzzer
  U2 = GAS_SENSOR [package=mq-3]

nets:
  N1: Composant1.A0, T1.Vout
  N2: Composant1.A1, U2.A1
  N3: Composant1.A2, U3.A1
  N4: Composant1.D21/SCL, Grove1.SDA
  N5: Composant1.D20/SDA, Grove1.SCL
  N6: Composant1.D9_PWM, Mod1.-
  VCC: Composant1.5V, U1.VCC, Grove1.VCC, Grove2.VCC, U3.H1, T1.+Vs, U2.H1
  GND: Composant1.GND, U1.GND, Grove1.GND, Grove2.GND, U3.H2, T1.GND, Mod1.S, U2.H2
  N7: Composant1.D0_RX0, U1.TXD
  N8: Composant1.D1_TX0, U1.RXD
  N9: U1.GPIO_4, Grove2.SCL
  N10: U1.GPIO_5, Grove2.SDA
